// Logisim project Logisim circuit file of 7 segment display.circ as structural Verilog: 1 circuit, main circuit 7 bar Combinational circuit
module _7_bar_Combinational_circuit (
  input  w,
  input  x,
  input  y,
  input  z,
  output a,
  output b,
  output c,
  output d,
  output e,
  output f,
  output g
);

  wire not_1_out, not_2_out, not_3_out, not_4_out, w_y_out, x_prime_w_y_out, x_prime_y_2_out, x_prime_y_out,
       x_prime_z_prime_out, x_y_prime_z_prime_out, xy_prime_z_out, xz_out, y_prime_z_prime_2_out,
       y_prime_z_prime_out, yz_out;

  not not_1 (not_1_out, w);
  not not_2 (not_2_out, x);
  not not_3 (not_3_out, y);
  not not_4 (not_4_out, z);
  and y_prime_z_prime (y_prime_z_prime_out, not_3_out, not_4_out);
  or y_prime_z_prime_2 (y_prime_z_prime_2_out, not_3_out, not_4_out);
  or x_prime_y (x_prime_y_out, not_2_out, y);
  and yz (yz_out, y, z);
  and xz (xz_out, x, z);
  and x_prime_z_prime (x_prime_z_prime_out, not_2_out, not_4_out);
  and x_prime_y_2 (x_prime_y_2_out, not_2_out, y);
  or w_y (w_y_out, w, y);
  and xy_prime_z (xy_prime_z_out, x, not_3_out, z);
  and x_y_prime_z_prime (x_y_prime_z_prime_out, y_prime_z_prime_2_out, x);
  and x_prime_y_z_prime (b, x_prime_y_out, not_4_out);
  and x_prime_w_y (x_prime_w_y_out, w_y_out, not_2_out);
  or or_1 (a, w, y_prime_z_prime_out, x_y_prime_z_prime_out);
  or or_2 (g, x_prime_w_y_out, b, xy_prime_z_out);
  or or_3 (c, not_2_out, yz_out, y_prime_z_prime_out);
  or or_4 (d, w, x, not_3_out, z);
  or or_5 (e, w, y, xz_out, x_prime_z_prime_out);
  or or_6 (f, w, x_y_prime_z_prime_out, x_prime_y_2_out);

  // Notes on the sheet:
  //   w
  //   w
  //   w
  //   w
  //   w
  //   w'
  //   x'
  //   x
  //   x'
  //   w'
  //   x
  //   x'
  //   w'
  //   x
  //   w'
  //   x'
  //   x
  //   w'
  //   x
  //   x'
  //   y
  //   y'
  //   z'
  //   z
  //   y
  //   y'
  //   z
  //   z'
  //   y
  //   y'
  //   z
  //   z'
  //   y'
  //   y
  //   z'
  //   z
  //   y'
  //   y
  //   z
  //   z'
endmodule
